// Logisim project WITCPU.circ as structural Verilog: 7 circuits, main circuit RegisterR10
module main (
);

  RAM #(.dataWidth(16)) ram_1 ();  // open: addr, data, sel, clk, ld, clr
endmodule

module RegisterR10 (
  input  [15:0] in_1,
  input  tick,
  input  [1:0] Ra,
  input  [1:0] in_4,
  input  [1:0] in_5,
  output [15:0] out_6,
  output [15:0] out_7
);

  wire demultiplexer_1_out0, demultiplexer_1_out1, demultiplexer_1_out2, demultiplexer_1_out3;
  wire [15:0] register_1_q, register_2_q, register_3_q, register_4_q;

  Demultiplexer #(.select(2)) demultiplexer_1 (
    .out0(demultiplexer_1_out0), .out1(demultiplexer_1_out1), .out2(demultiplexer_1_out2),
    .out3(demultiplexer_1_out3), .in(tick), .sel(in_4));  // open: en
  Register #(.width(16)) register_1 (.D({16{1'b0}}), .Q(register_1_q), .clk(demultiplexer_1_out0));  // open: en, clr
  Register #(.width(16)) register_2 (.D(in_1), .Q(register_2_q), .clk(demultiplexer_1_out1));  // open: en, clr
  Register #(.width(16)) register_3 (.D(in_1), .Q(register_3_q), .clk(demultiplexer_1_out2));  // open: en, clr
  Register #(.width(16)) register_4 (.D(in_1), .Q(register_4_q), .clk(demultiplexer_1_out3));  // open: en, clr
  Multiplexer #(.select(2), .width(16)) multiplexer_1 (
    .in0(register_1_q), .in1(register_2_q), .in2(register_3_q), .in3(register_4_q), .out(out_6), .sel(Ra));  // open: en
  Multiplexer #(.select(2), .width(16)) multiplexer_2 (
    .in0(register_1_q), .in1(register_2_q), .in2(register_3_q), .in3(register_4_q), .out(out_7), .sel(in_5));  // open: en
endmodule

module group (
  input  [15:0] in_1,
  input  tick,
  input  [1:0] in_3,
  input  [1:0] in_4,
  input  [1:0] in_5,
  output [15:0] out_6,
  output [15:0] out_7
);

  wire demultiplexer_1_out0, demultiplexer_1_out1, demultiplexer_1_out2, demultiplexer_1_out3;
  wire [15:0] register_1_q, register_2_q, register_3_q, register_4_q;

  Demultiplexer #(.select(2)) demultiplexer_1 (
    .out0(demultiplexer_1_out0), .out1(demultiplexer_1_out1), .out2(demultiplexer_1_out2),
    .out3(demultiplexer_1_out3), .in(tick), .sel(in_4));  // open: en
  Register #(.width(16)) register_1 (.D(in_1), .Q(register_1_q), .clk(demultiplexer_1_out0));  // open: en, clr
  Register #(.width(16)) register_2 (.D(in_1), .Q(register_2_q), .clk(demultiplexer_1_out1));  // open: en, clr
  Register #(.width(16)) register_3 (.D(in_1), .Q(register_3_q), .clk(demultiplexer_1_out2));  // open: en, clr
  Register #(.width(16)) register_4 (.D(in_1), .Q(register_4_q), .clk(demultiplexer_1_out3));  // open: en, clr
  Multiplexer #(.select(2), .width(16)) multiplexer_1 (
    .in0(register_1_q), .in1(register_2_q), .in2(register_3_q), .in3(register_4_q), .out(out_6), .sel(in_3));  // open: en
  Multiplexer #(.select(2), .width(16)) multiplexer_2 (
    .in0(register_1_q), .in1(register_2_q), .in2(register_3_q), .in3(register_4_q), .out(out_7), .sel(in_5));  // open: en
endmodule

module ALU (
  input  Enable,
  input  [3:0] opcode,
  input  [15:0] x,
  input  [15:0] y,
  input  [7:0] imm,
  output [15:0] out_6
);

  wire [15:0] adder_1_out, and_1_out, divider_1_out, multiplier_1_out, or_1_out, subtractor_1_out, xnor_1_out;

  Adder #(.width(16)) adder_1 (.a(x), .b(y), .out(adder_1_out));  // open: cin, cout
  Subtractor #(.width(16)) subtractor_1 (.a(x), .b(y), .out(subtractor_1_out));  // open: bin, bout
  Multiplier #(.width(16)) multiplier_1 (.a(x), .b(y), .out(multiplier_1_out));  // open: cin, cout
  Divider #(.width(16)) divider_1 (.a(x), .b(y), .out(divider_1_out));  // open: upper, rem
  assign and_1_out = x & y;  // AND_Gate and_1, 16 bits wide
  assign or_1_out = x | y;  // OR_Gate or_1, 16 bits wide
  assign xnor_1_out = ~(x ^ y);  // XNOR_Gate xnor_1, 16 bits wide
  Multiplexer #(.select(3), .width(16)) multiplexer_1 (
    .in0(adder_1_out), .in1(subtractor_1_out), .in2(multiplier_1_out), .in3(divider_1_out), .in4(and_1_out),
    .in5(or_1_out), .in6(xnor_1_out), .in7({{9{imm[7]}}, imm[6:0]}), .out(out_6), .sel(opcode[2:0]),
    .en(Enable));
endmodule

module Decoder (
  input  [15:0] \input ,
  output [3:0] opcode,
  output [3:0] Rx,
  output [3:0] Rd,
  output [3:0] Ry,
  output [7:0] mm
);

  Multiplexer #(.width(4)) multiplexer_1 (
    .in0(\input [3:0]), .in1(\input [7:4]), .out(Ry), .sel(\input [15]));  // open: en

  assign mm = \input [7:0];
  assign opcode = \input [15:12];
  assign Rd = \input [7:4];
  assign Rx = \input [11:8];
endmodule

module PC_Controller (
  input  [15:0] Rx,
  input  [3:0] opcode,
  input  [7:0] imm,
  input  [7:0] prev,
  output [7:0] out_5
);

  wire and_1_out, comparator_1_eq, comparator_1_gt, comparator_1_lt, multiplexer_1_out, not_1_out, not_2_out;
  wire [7:0] adder_1_out;

  Comparator #(.width(16)) comparator_1 (
    .a(Rx), .b({16{1'b0}}), .gt(comparator_1_gt), .eq(comparator_1_eq), .lt(comparator_1_lt));
  Adder adder_1 (.a(prev), .b({8{1'b0}}), .out(adder_1_out));  // open: cin, cout
  not not_1 (not_1_out, comparator_1_eq);
  Multiplexer #(.select(2)) multiplexer_1 (
    .in0(comparator_1_eq), .in1(not_1_out), .in2(comparator_1_gt), .in3(comparator_1_lt),
    .out(multiplexer_1_out), .sel(opcode[1:0]));  // open: en
  not not_2 (not_2_out, opcode[2]);
  and and_1 (and_1_out, multiplexer_1_out, not_2_out, opcode[3]);
  Multiplexer #(.width(8)) multiplexer_2 (.in0(adder_1_out), .in1(imm), .out(out_5), .sel(and_1_out));  // open: en
endmodule

module Clock (
  output out_1
);

  wire not_1_out;

  Clock_part clock_1 (.out(out_1));
  not not_1 (not_1_out, out_1);
  T_Flip_Flop t_ff_1 (.clk(not_1_out), .T(1'b1));  // open: Q, Qn, preset, reset, en
endmodule
